# Fritzing sketch sketch1 (saved by Fritzing 0.9.3b)
breadboards: 1

parts:
  Part1 = Arduino Nano (Rev3.0) (ICSP)
  GSM_SIM_GPSR_SMS_SIM900_SIM1 = SIM800L [package=THT]
  DS1 = DS18B20 1-Wire Temperature Sensor [part_number=DS18B20]

nets:
  GND: Part1.GND, GSM_SIM_GPSR_SMS_SIM900_SIM1.GND#1, DS1.GND
  N1: Part1.D2, DS1.DQ
  N2: Part1.D11/MOSI, GSM_SIM_GPSR_SMS_SIM900_SIM1.SIM_RXD
  N3: Part1.D12/MISO, GSM_SIM_GPSR_SMS_SIM900_SIM1.SIM_TXD
  5V: Part1.5V, GSM_SIM_GPSR_SMS_SIM900_SIM1.5V, DS1.VDD
